# Fritzing sketch Rasp (saved by Fritzing 0.9.3b)
breadboards: 1

parts:
  Raspberry_Pi_1 = Raspberry Pi 3 [part_number=RPI-3-V1.2]  # not connected
  Part1 = Adafruit Pi Cobbler Plus [part_number="Adafruit #2029"]  # not connected
  KEYPAD3 = Membrane Matrix Keypad  # not connected
  U2 = LCD-16X2 [package=lcd-16x2_noholes]
  U4 = POT [package=pot_mammoth]

nets:
  N1: U2.VSS, U2.R_W, U4.S
  N2: U2.VDD, U4.E
  N3: U2.VO, U4.A

custom parts:
  Adafruit Pi Cobbler Plus: The Raspberry Pi B+/Pi 2/ Pi 3 has landed on the Maker World like a 40-GPIO pinned, quad-USB ported, credit card sized bomb of DIY joy. And while you can use most of our great Model B accessories by hooking up our downgrade cable, its probably a good time to upgrade your set up and accessorize using all of the Model B+'s / Pi 2's / Pi 3's 40 pins. That's why we now carry the Adafruit Assembled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
  Membrane Matrix Keypad: Membrane Matrix 3x4 Keypad
